# Fritzing sketch syringe (saved by Fritzing 0.9.2b)
breadboards: 1

parts:
  Part1 = Arduino Uno (Rev3) - ICSP
  Syringe = Stepper Motor - Bipolar
  start = Momentary Switch [package=ksa_sealed_tac_switch]
  Reset = Momentary Switch [package=ksa_sealed_tac_switch]
  Part2 = EasyDriver_v44
  Retracted = Momentary Switch [package=ksa_sealed_tac_switch]
  Extended = Momentary Switch [package=ksa_sealed_tac_switch]
  GND1 = Header 1 [package=1x01_offset]
  GND2 = Header 1 [package=1x01_offset]
  C1 = Capacitor [part_number=100muF package=cap-pth-small]
  BAT1 = Battery Holders [part_number="12V Power Supply" package=battery-aaa]

nets:
  GND: Part1.GND, start.4, Reset.4, Part2.GND, Part2.V+, C1.1, C1.2, BAT1.-, BAT1.+
  N1: Part1.D2, Reset.2
  N2: Part1.D3_PWM, Part2.STEP
  N3: Part1.D4, Part2.DIR
  N4: Part1.D5_PWM, start.2
  N5: Part1.D6_PWM, Retracted.2
  N6: Part1.D7, Extended.2
  5V: Part1.5V, Part2.VCC
  N7: Syringe.A, Part2.OUT2A
  N8: Syringe.C, Part2.OUT2B
  N9: Syringe.B, Part2.OUT1A
  N10: Syringe.D, Part2.OUT1B
  N11: Retracted.4, GND2.1
  N12: Extended.4, GND1.1

notes:
  12V Side
  5V Side
  wiring is wrong on this drawing.
  Schematic is useless when I look at it
  Driver Board probably not same as yours. May require more pins (enable?)
